# Fritzing sketch Automacao_com_arduino_bluetooth_aulaV_IOT (saved by Fritzing 0.9.3b)
breadboards: 1

parts:
  Componente1 = Arduino Uno (Rev3)
  Componente2 = Bluetooth HC-05 Macho
  R3 = Resistor [tolerance=±5% resistance=2.2k package=THT]
  R4 = Resistor [tolerance=±5% resistance=1k package=THT]
  hc-sr1 = hc-sr04

nets:
  N1: Componente1.D12/MISO, hc-sr1.Trig
  N2: Componente1.D13/SCK, hc-sr1.Echo
  GND: Componente1.GND, Componente2.GND, R3.Pin_1, hc-sr1.GND
  N3: Componente1.D2, Componente2.TXD
  N4: Componente1.D3_PWM, R4.Pin_0
  VCC: Componente1.5V, Componente2.VCC, hc-sr1.VCC
  N5: Componente2.RXD, R3.Pin_0, R4.Pin_1
