# Fritzing sketch Untitled Sketch 2 (saved by Fritzing 0.9.3b)
breadboards: 1

parts:
  Componente1 = Arduino Uno (Rev3)
  R1 = Resistor [tolerance=±5% resistance=220 package=THT]
  R2 = Resistor [tolerance=±5% resistance=220 package=THT]
  LED1 = LED - 5mm [color="Red (633nm)" package="5 mm [THT]"]
  LED2 = LED - 5mm [color="Red (633nm)" package="5 mm [THT]"]

nets:
  N1: Componente1.D12/MISO, LED2.anode
  N2: Componente1.D13/SCK, LED1.anode
  N3: Componente1.GND, R1.Pin_1, R2.Pin_1
  N4: R1.Pin_0, LED1.cathode
  N5: R2.Pin_0, LED2.cathode
