# Fritzing sketch Automacao_com_arduino_bluetooth_aulaIV (saved by Fritzing 0.9.3b)
breadboards: 1

parts:
  Componente1 = Arduino Uno (Rev3)
  R1 = Resistor [tolerance=±5% resistance=220 package=THT]
  LED1 = LED - 5mm [color="Red (633nm)" package="5 mm [THT]"]
  Componente2 = Bluetooth HC-05 Macho
  R3 = Resistor [tolerance=±5% resistance=2.2k package=THT]
  R4 = Resistor [tolerance=±5% resistance=1k package=THT]
  Q1 = Basic FET P-Channel [package="TO220 [THT]"]
  D1 = Rectifier Diode [part_number=1N4001 package="300 mil [THT]"]  # not connected
  R5 = Resistor [tolerance=±5% resistance=1k package=THT]
  OMRON1 = OMRON PCB Power Relay – G5LE [part_number="G5LE-1\n" package=THT]

nets:
  N1: Componente1.D12/MISO, R5.Pin_0
  N2: Componente1.D13/SCK, LED1.anode
  N3: Componente1.D2, Componente2.TXD
  N4: Componente1.D3_PWM, R4.Pin_0
  5V: Componente1.5V, Componente2.VCC, OMRON1.COIL1
  GND: Componente1.GND, R1.Pin_1, Componente2.GND, R3.Pin_1, Q1.source
  N5: R1.Pin_0, LED1.cathode
  N6: Componente2.RXD, R3.Pin_0, R4.Pin_1
  N7: Q1.gate, R5.Pin_1
  N8: Q1.drain, OMRON1.COIL2
