# Fritzing sketch leitura_analogica (saved by Fritzing 0.9.3b)
breadboards: 1

parts:
  R1 = Resistor [tolerance=±5% resistance=10k package=THT]
  R2 = Photocell (LDR) [package=THT]
  Componente1 = Arduino Uno (Rev3)

nets:
  N1: R1.Pin_0, R2.pin_0, Componente1.A0
  N2: R1.Pin_1, R2.pin_1, Componente1.GND
