# Fritzing sketch Servo_motor (saved by Fritzing 0.9.3b)

parts:
  J1 = Basic Servo
  Componente1 = Arduino Uno (Rev3)

nets:
  GND: J1.gnd, Componente1.GND
  VCC: J1.vcc, Componente1.5V
  N1: J1.pulse, Componente1.D9_PWM
