# Fritzing sketch ldr (saved by Fritzing 0.9.3b)
breadboards: 1

parts:
  Componente1 = Arduino Uno (Rev3)
  LED1 = LED - 5mm [color="Red (633nm)" package="5 mm [THT]"]
  R1 = Resistor [tolerance=±5% resistance=330 package=THT]
  R2 = Photocell (LDR) [package=THT]
  R3 = Resistor [tolerance=±5% resistance=10k package=THT]

nets:
  N1: Componente1.A0, R2.pin_0, R3.Pin_0
  N2: Componente1.D13/SCK, LED1.anode
  N3: Componente1.5V, R2.pin_1
  N4: Componente1.GND, R1.Pin_1, R3.Pin_1
  N5: LED1.cathode, R1.Pin_0
