# Fritzing sketch leitura_analogica_led (saved by Fritzing 0.9.3b)
breadboards: 1

parts:
  R1 = Resistor [tolerance=±5% resistance=10k package=THT]
  R2 = Photocell (LDR) [package=THT]
  Componente1 = Arduino Uno (Rev3)
  R3 = Resistor [tolerance=±5% resistance=220 package=THT]
  LED1 = LED - 5mm [color="White (4500K)" package="5 mm [THT]"]

nets:
  N1: R1.Pin_0, R2.pin_0, Componente1.A0
  N2: R1.Pin_1, R2.pin_1, Componente1.GND, R3.Pin_0
  N3: Componente1.D2, LED1.anode
  N4: R3.Pin_1, LED1.cathode
