# Fritzing sketch superMaquina_final (saved by Fritzing 0.9.3b)
circuit board: 8.46667cm x 5.64444cm
breadboards: 1

parts:
  Supermaquina = Arduino Uno (Rev3)
  LED2 = LED - 5mm [color="Red (633nm)" package="5 mm [THT]"]
  LED4 = LED - 5mm [color="Red (633nm)" package="5 mm [THT]"]
  R5 = Resistor [tolerance=±5% resistance=330 package=THT]
  LED3 = LED - 5mm [color="Red (633nm)" package="5 mm [THT]"]
  R1 = Resistor [tolerance=±5% resistance=330 package=THT]
  LED5 = LED - 5mm [color="Red (633nm)" package="5 mm [THT]"]
  R4 = Resistor [tolerance=±5% resistance=330 package=THT]
  R3 = Resistor [tolerance=±5% resistance=330 package=THT]
  R2 = Resistor [tolerance=±5% resistance=330 package=THT]
  LED1 = LED - 5mm [color="Red (633nm)" package="5 mm [THT]"]

nets:
  N1: Supermaquina.D9_PWM, LED5.anode
  N2: Supermaquina.D10_PWM/SS, LED4.anode
  N3: Supermaquina.D11_PWM/MOSI, LED3.anode
  N4: Supermaquina.D12/MISO, LED2.anode
  N5: Supermaquina.D13/SCK, LED1.anode
  N6: Supermaquina.GND, R5.Pin_1, R1.Pin_1, R4.Pin_1, R3.Pin_1, R2.Pin_1
  N7: LED2.cathode, R2.Pin_0
  N8: LED4.cathode, R4.Pin_0
  N9: R5.Pin_0, LED5.cathode
  N10: LED3.cathode, R3.Pin_0
  N11: R1.Pin_0, LED1.cathode

notes:
  Projeto Supermáquina

// code stored in the sketch: Spermaquina_dias.ino
/**
   Sequencial de LEDs (efeito supermáquina)
   @author-Fabio Dias
*/
void setup() {
  pinMode(13, OUTPUT);
  pinMode(12, OUTPUT);
  pinMode(11, OUTPUT);
  pinMode(10, OUTPUT);
  pinMode(9, OUTPUT);
}

void loop() {
 int efeito = 50;
 for (int i=13; i>=9; i--){
  digitalWrite (i, HIGH);
  delay (efeito);
  digitalWrite(i, LOW);
 }
 for (int i=10; i<=12; i++){
  digitalWrite (i, HIGH);
  delay (efeito);
  digitalWrite(i, LOW);
 }
}
